# Fritzing sketch ArduinoFlightControllStick (saved by Fritzing 0.9.3b)
breadboards: 1

parts:
  U1 = PCF8574 [package="DIP16 [THT]"]
  Part1 = Arduino Micro (Rev3)
  S1 = Pushbutton [package="[THT]"]
  S2 = Pushbutton [package="[THT]"]
  S3 = Pushbutton [package="[THT]"]
  S4 = Pushbutton [package="[THT]"]
  S5 = Pushbutton [package="[THT]"]
  S6 = Pushbutton [package="[THT]"]
  S7 = Pushbutton [package="[THT]"]
  S8 = Pushbutton [package="[THT]"]
  S9 = Pushbutton [package="[THT]"]
  R1 = Resistor [tolerance=±1% resistance=10k package=THT]
  R2 = Resistor [tolerance=±1% resistance=10k package=THT]
  R3 = Resistor [tolerance=±1% resistance=10k package=THT]
  R4 = Resistor [tolerance=±1% resistance=10k package=THT]
  R5 = Resistor [tolerance=±1% resistance=10k package=THT]
  R6 = Resistor [tolerance=±1% resistance=10k package=THT]
  R7 = Resistor [tolerance=±1% resistance=10k package=THT]
  R8 = Resistor [tolerance=±1% resistance=10k package=THT]

nets:
  VCC: U1.A3, U1.P0, U1.P1, U1.P2, U1.P4, U1.P6, U1.P7, U1.VCC, Part1.D7, Part1.5V, S2.Pin_3, S2.Pin_4, S3.Pin_3, S3.Pin_4, S4.Pin_3, S4.Pin_4, S5.Pin_3, S5.Pin_4, S6.Pin_3, S6.Pin_4, S7.Pin_3, S7.Pin_4, S8.Pin_3, S8.Pin_4, S9.Pin_3, S9.Pin_4
  GND: U1.P3, U1.GND, Part1.GND, S1.Pin_3, S1.Pin_4, R1.Pin_0, R2.Pin_0, R3.Pin_0, R4.Pin_0, R5.Pin_0, R6.Pin_0, R7.Pin_0, R8.Pin_0
  N1: U1.P5, S2.Pin_1, S2.Pin_2, R6.Pin_1
  N2: S1.Pin_1, S1.Pin_2, R5.Pin_1
  N3: S3.Pin_1, S3.Pin_2, R7.Pin_1
  N4: S4.Pin_1, S4.Pin_2, R8.Pin_1
  N5: S5.Pin_1, S5.Pin_2, R1.Pin_1
  N6: S6.Pin_1, S6.Pin_2
  N7: S7.Pin_1, S7.Pin_2, R4.Pin_1
  N8: S8.Pin_1, S8.Pin_2, R3.Pin_1
  N9: S9.Pin_1, S9.Pin_2, R2.Pin_1
