# Fritzing sketch Pi PSU layout (saved by Fritzing 0.9.2b)
breadboards: 1

parts:
  Raspberry_Pi1 = Raspberry Pi 2
  V1 = DC Power [voltage=5V]
  R1 = Resistor [tolerance=±5% resistance=10k package=THT]
  R2 = Resistor [tolerance=±5% resistance=47k package=THT]
  R3 = Resistor [tolerance=±5% resistance=220 package=THT]
  S1 = Pushbutton [package=THT]
  S2 = Pushbutton [package=THT]
  Q1 = NPN-Transistor [package="TO92 [THT]"]
  Q2 = NPN-Transistor [package="TO92 [THT]"]
  C1 = Electrolytic Capacitor [capacitance=1µF package="100 mil [THT, electrolytic]"]
  D1 = Rectifier Diode [part_number=1N4001 package="300 mil [THT]"]
  D2 = Rectifier Diode [part_number=1N4001 package="300 mil [THT]"]
  R4 = Resistor [tolerance=±5% resistance=10k package=THT]
  U1 = RELAY [package=relay-g5q]
  K1 = Relay [part_number=FRS1B-S package=THT]  # not connected

nets:
  N1: Raspberry_Pi1.GND, V1.V-, R3.Pin_0, S2.leg1, Q2.E, C1.-
  N2: Raspberry_Pi1.GPIO14, D1.anode
  N3: Raspberry_Pi1.5V, S1.leg0, D2.cathode, U1.NO, U1.COIL1
  N4: V1.V+, S1.leg1, U1.MAIN
  N5: R1.Pin_0, D1.cathode
  N6: R1.Pin_1, R2.Pin_0, R3.Pin_1, R4.Pin_0
  N7: R2.Pin_1, U1.NC
  N8: S2.leg0, Q1.B, C1.+, R4.Pin_1
  N9: Q1.E, Q2.B
  N10: Q1.C, Q2.C, D2.anode, U1.COIL2
