# Fritzing sketch TankSchematic (saved by Fritzing 0.9.3b)
perfboards: 2

parts:
  Part1 = Arduino Mega 2560 (Rev3)
  MD03A1 = Dual VNH2SP30 Motor Driver [part_number=MD03A]
  M1 = DC Motor
  M2 = DC Motor
  U1 = LIPO-110mAh [package=lipo-110]
  U3 = LIPO-110mAh [package=lipo-110]
  U4 = LIPO-110mAh [package=lipo-110]
  J1 = Basic Servo
  J2 = Basic Servo
  Part5 = 10-DOF IMU L3GD20H + LSM303 + BMP180 [part_number=1604]
  J5 = female pin header, 3 pins [form="♀ (female)"]
  J6 = female pin header, 3 pins [form="♀ (female)"]
  J7 = female pin header, 4 pins [form="♀ (female)"]
  Part6 = nodeMCU LoLin
  Part7 = Logic Level Converter
  Part8 = Bluetooth HC-05 Macho
  C1 = Ceramic Capacitor [capacitance=100nF package="100 mil [THT, multilayer]"]
  J8 = female pin header, 6 pins [form="♀ (female)"]
  R1 = Resistor [tolerance=±5% resistance=15k package=THT]
  R2 = Resistor [tolerance=±5% resistance=10k package=THT]
  R3 = Resistor [tolerance=±5% resistance=2.2k package=THT]

nets:
  N1: Part1.A0, MD03A1.1CS
  N2: Part1.A1, MD03A1.2CS
  N3: Part1.D21/SCL, Part5.SCL
  N4: Part1.D20/SDA, Part5.SDA
  N5: Part1.D15/RX3, Part7.RX2_HV
  GND: Part1.GND, MD03A1.GND#136, Part5.GND, J7.pin1, Part6.GND#29, Part8.GND, J8.pin3
  N6: Part1.D9_PWM, J7.pin4
  N7: Part1.D8_PWM, J7.pin3
  N8: Part1.RESET, C1.0, R1.Pin_0, R2.Pin_1
  VIN: Part1.5V, MD03A1.+5V_(IN), Part5.VIN, J7.pin2, Part6.Vin, Part8.VCC, J8.pin2
  N9: Part1.VIN, MD03A1.VIN#139
  N10: Part1.D3_PWM, MD03A1.PWM
  N11: Part1.D5_PWM, MD03A1.2PWM
  N12: Part1.D30, MD03A1.1DIAG/EN
  N13: Part1.D31, MD03A1.2DIAG/EN
  N14: Part1.D32, MD03A1.1INa
  N15: Part1.D33, MD03A1.2INb#142
  N16: Part1.D34, MD03A1.1INb
  N17: Part1.D35, MD03A1.2INb#143
  N18: MD03A1.OUT_1A, M2.pin_1
  N19: MD03A1.OUT_1B, M2.pin_2
  N20: MD03A1.OUT_2A, M1.pin_1
  N21: MD03A1.OUT_2B, M1.pin_2
  N22: MD03A1.VIN#150, U4.+
  N23: MD03A1.GND#151, U1.-
  N24: U1.+, U3.-
  N25: U3.+, U4.-
  N26: J1.gnd, J5.pin1
  N27: J1.vcc, J5.pin2
  N28: J1.pulse, J5.pin3
  N29: J2.gnd, J6.pin1
  N30: J2.vcc, J6.pin2
  N31: J2.pulse, J6.pin3
  N32: Part6.VU, Part6.D10
  N33: Part6.S3, Part6.GND#32
  N34: Part6.D6, Part7.TX2_LV
  N35: Part6.D5, Part7.RX2_LV
  N36: Part6.G, Part7.GND
  N37: Part6.3V#40, Part7.LV
  N38: Part7.RX_LV, R3.Pin_1
  N39: Part8.State, J8.pin6
  N40: Part8.TXD, J8.pin4
  N41: Part8.RXD, J8.pin5

custom parts:
  10-DOF IMU L3GD20H + LSM303 + BMP180: This inertial-measurement-unit combines 3 of the best quality sensors available on the market to give you 11 axes of data: 3 axes of accelerometer data, 3 axes gyroscopic, 3 axes magnetic (compass), barometric pressure/altitude and temperature. We tested many different 'combination' sensors and found these were the best value, with stable and reliable readings.
  nodeMCU LoLin: LoLin is a tiny board, based on ESP8266, integates GPIO, PWM, IIC, 1-Wire and ADC all in one board. It's base on NodeMCU, A lua based firmware for wifi-soc esp8266 Build on ESP8266 sdk Lua core based on eLua project cjson based on lua-cjson File system based on spiffs Easy to access wireless router Based on Lua 5.1.4 (without debug, os module.) Event-Drive programming preferred. Build-in json,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

// code stored in the sketch: BattleBotServerArduino.ino
/*
 Name:		BattleBotServerArduino.ino
 Created:	10/9/2016 3:08:15 PM
 Author:	Natsuki
*/

// the setup function runs once when you press reset or power the board

#include <TimedAction.h>
#include <Adafruit_BMP085_U.h>
#include <Adafruit_Sensor.h>
#include <Adafruit_L3GD20_U.h>
#include <Adafruit_LSM303_U.h>
#include <MahonyAHRS.h>
#include <Servo.h>
//#include <ThreadController.h>
//#include <TimerOne.h>
#include "BattleBotComBytes.h"
#include <DualVNH5019MotorShieldMega.h>

#define ESPSTATUSLED	24 // Lights up when a client has connected to the ESP
#define ESPRESETPIN	45	 // This connects to the ESP reset pin incase it won't work
// Shoot section
#define SHOOTPIN		20 // Here the transistor is connected for the shooting
#define LASERPIN		21 // This is where the laser for the ammo detection is.
#define LASERDETECTPIN	22 // This is where the phototransistor for the laser is.

#define PANSERVOPIN		8
#define TILTSERVOPIN    9
byte DC1MotorSpeedSerial, DC2MotorSpeedSerial, panSerial, tiltSerial;
int DC1MotorSpeed, DC2MotorSpeed, pan, tilt;

DualVNH5019MotorShield Motors = DualVNH5019MotorShield(32, 34, 30, A0, 33, 35, 31, A1);
Servo panServo, tiltServo, shootServo;

// Create sensor instances.
Adafruit_L3GD20_Unified       gyro(20);
Adafruit_LSM303_Accel_Unified accel(30301);
Adafruit_LSM303_Mag_Unified   mag(30302);
Adafruit_BMP085_Unified       bmp(18001);


float seaLevelPressure, altitude, temperature;
byte M1Current, M2Current;

//ThreadController threadController = ThreadController();
//Thread dofthread = Thread();
//Thread connectionThread = Thread();

volatile int timeSinceLastReceivedMotorData = 0;
unsigned long previousMillis = millis();
unsigned long currentMillis = millis();
bool clientConnected;
byte buffer[10];

//void timerCallback()
//{
//	threadController.run();
//}


float mag_offsets[3] = { -7.07F, 9.55F, -28.22F };

float mag_softiron_matrix[3][3] = { { 0.955, 0.009, 0.004 },
{ 0.009, 0.930, -0.034 },
{ -0.004, -0.034, 1.127 } };

float mag_field_strength = 54.82F;

Mahony filter;




float roll, heading, pitch;

void getDofData()
{
	sensors_event_t gyro_event;
	sensors_event_t accel_event;
	sensors_event_t mag_event;
	sensors_event_t bmp_event;
	// Get new data samples
	gyro.getEvent(&gyro_event);
	accel.getEvent(&accel_event);
	mag.getEvent(&mag_event);
	bmp.getEvent(&bmp_event);

	// Apply mag offset compensation (base values in uTesla)
	float x = mag_event.magnetic.x - mag_offsets[0];
	float y = mag_event.magnetic.y - mag_offsets[1];
	float z = mag_event.magnetic.z - mag_offsets[2];

	// Apply mag soft iron error compensation
	float mx = x * mag_softiron_matrix[0][0] + y * mag_softiron_matrix[0][1] + z * mag_softiron_matrix[0][2];
	float my = x * mag_softiron_matrix[1][0] + y * mag_softiron_matrix[1][1] + z * mag_softiron_matrix[1][2];
	float mz = x * mag_softiron_matrix[2][0] + y * mag_softiron_matrix[2][1] + z * mag_softiron_matrix[2][2];

	// The filter library expects gyro data in degrees/s, but adafruit sensor
	// uses rad/s so we need to convert them first (or adapt the filter lib
	// where they are being converted)
	float gx = gyro_event.gyro.x * 57.2958F;
	float gy = gyro_event.gyro.y * 57.2958F;
	float gz = gyro_event.gyro.z * 57.2958F;
	// Update the filter
	filter.update(gx, gy, gz,
		accel_event.acceleration.x, accel_event.acceleration.y, accel_event.acceleration.z,
		mx, my, mz);

	roll = filter.getRoll();
	pitch = filter.getPitch();
	heading = filter.getYaw();

	Serial.print(millis());
	Serial.print(" - Orientation: ");
	Serial.print(heading);
	Serial.print(" ");
	Serial.print(pitch);
	Serial.print(" ");
	Serial.println(roll);
}

void connectionHandler() // This is to make sure the tank doesn't go haywire when the ESP stops working
{
	if (currentMillis - previousMillis > 50 && clientConnected == true)
	{
		Serial.println("Didn't recieve data in time from the ESP");
		Motors.setBrakes(0, 0); // In case of connection troubles. We do not reset the esp YET
	}
	if (currentMillis - previousMillis > 500 && clientConnected == true)
	{
		Motors.setBrakes(0, 0);
		digitalWrite(ESPRESETPIN, HIGH);
		delay(2);
		digitalWrite(ESPRESETPIN, LOW);
	}
}


TimedAction dofThread = TimedAction(50, getDofData);
TimedAction connectionThread = TimedAction(30, connectionHandler);


void setup()
{
	Serial.begin(115200);
	Serial3.begin(250000);

	if (!gyro.begin())
	{
		/* There was a problem detecting the L3GD20 ... check your connections */
		Serial.println("Ooops, no L3GD20 detected ... Check your wiring!");
		while (1);
	}

	if (!accel.begin())
	{
		/* There was a problem detecting the LSM303DLHC ... check your connections */
		Serial.println("Ooops, no L3M303DLHC accel detected ... Check your wiring!");
		while (1);
	}

	if (!mag.begin())
	{
		/* There was a problem detecting the LSM303DLHC ... check your connections */
		Serial.println("Ooops, no L3M303DLHC mag detected ... Check your wiring!");
		while (1);
	}
	if(!bmp.begin())
	{
		Serial.println("Ooops, no BMP085 detected ... Check your wiring!");
		while (1);
	}
	// Threading things
//	dofthread.onRun(getDofData);
//	dofthread.setInterval(100);
//	threadController.add(&dofthread);
//	connectionThread.onRun(connectionHandler);
//	connectionThread.setInterval(30);
//	threadController.add(&connectionThread);
//	Timer1.initialize(20000);
//	Timer1.attachInterrupt(timerCallback);
//	Timer1.start();
	// Threading things done
	filter.begin(20);
	panServo.attach(PANSERVOPIN);
	tiltServo.attach(TILTSERVOPIN);
	panServo.write(90);
	tiltServo.write(90);
	Motors.init();
	Wire.begin();

	Serial.println("Ready");
}

void MoveMotors()
{
	M1Current = Motors.getM1CurrentMilliamps() / 1000;
	M2Current = Motors.getM2CurrentMilliamps() / 1000;
	if (!Motors.getM1Fault()) {// Check if there is a fault in the motor driver on M1
		if (M1Current < 16)
		{ // Check if the current isn't to high
			Motors.setM1Speed(DC1MotorSpeed);
		}
		else
		{
			Serial.println("Warning: Motor 1 current is to high");
			if (Serial3.availableForWrite())
			{
				Serial3.write(ESPMOTORDIAG);
				Serial3.write(MOTOR1);
				Serial3.write(CURRENTWARNING);
				Serial3.write(MESSAGEEND);
			}
			Motors.setBrakes(0, 0);
		}
	}
	else
	{
		Serial.println("Warning: Motor 1 has a fault");

		if (Serial3.availableForWrite()) {
			Serial3.write(ESPMOTORDIAG);
			Serial3.write(MOTOR1);
			Serial3.write(MOTORFAULT);
			Serial3.write(MESSAGEEND);
		}
		Motors.setBrakes(0, 0);
	}
	if (!Motors.getM2Fault()) {// Check if there is a fault in the motor driver on M1
		if (M2Current < 16)
		{ // Check if the current isn't to high
			Motors.setM2Speed(DC2MotorSpeed);
		}
		else
		{
			Serial.println("Warning: Motor 2 current is to high");
			if (Serial3.availableForWrite())
			{
				Serial3.write(ESPMOTORDIAG);
				Serial3.write(MOTOR2);
				Serial3.write(CURRENTWARNING);
				Serial3.write(MESSAGEEND);
			}
			Motors.setBrakes(0, 0);
		}
	}
	else
	{
		Serial.println("Warning: Motor 2 has a fault");
		if (Serial3.availableForWrite()) {
			Serial3.write(ESPMOTORDIAG);
			Serial3.write(MOTOR2);
			Serial3.write(MOTORFAULT);
			Serial3.write(MESSAGEEND);
		}
		Motors.setBrakes(0, 0);
	}
}
#pragma region ReadSerialData
bool EndMessage()
{
	if (Serial3.read() == MESSAGEEND) return true;
	return false;
}

void ReadMotorData()
{
	DC1MotorSpeedSerial = Serial3.read();
	DC2MotorSpeedSerial = Serial3.read();
	byte endCommand = Serial3.read();
	Serial.print(DC1MotorSpeedSerial);
	Serial.print(" ");
	Serial.print(DC2MotorSpeedSerial);
	Serial.print(" ");
	Serial.println(endCommand);
	if (endCommand == MESSAGEEND)
	{
		DC1MotorSpeed = map(DC1MotorSpeedSerial, 0, 200, -400, 400);
		DC2MotorSpeed = map(DC2MotorSpeedSerial, 0, 200, -400, 400);
		Serial.print(DC1MotorSpeed);
		Serial.print(" ");
		Serial.println(DC2MotorSpeed);
		if (clientConnected)
		{ // Just to be on the safe side
			MoveMotors();
		}
		previousMillis = millis();
	}
	else
	{// Command not recieved
		Serial.println("Motor data is not valid");
	}
}

void ReadServoData()
{
	panSerial = Serial3.read();
	tiltSerial = Serial3.read();
	Serial.print(panSerial, HEX);
	Serial.print(" ");
	Serial.print(tiltSerial, HEX);
	Serial.print(" ");
	if (EndMessage())
	{
		pan = map(panSerial, 0, 200, 0, 180);
		tilt = map(tiltSerial, 0, 200, 0, 180);
		panServo.write(pan);
		tiltServo.write(tilt);
	}
	else
	{
		Serial.write("Error getting the pantilt values");
	}
}

void ReadGenericData()
{
	byte command = Serial3.read();
	switch (command)
	{
	case GENSHOOT: // Right now it's just a laser that shoots and that is handled by the Mega itself
		if (EndMessage())
		{
			digitalWrite(LASERPIN, HIGH);
			delay(3);
			digitalWrite(LASERPIN, LOW);
		}
		break;
	default: break;
	}
}

void ReadClientData()
{
	byte espclientmessage = Serial3.read();
	if (espclientmessage == CLIENTESPREADY)
	{
		if (EndMessage())
		{
			Serial.println("ESP is ready for data");
		}
	}
	else if (espclientmessage == CLIENTCONNECT)
	{
		if (EndMessage())
			Serial.println("A client has connected");
		clientConnected = true;
	}
	else if (espclientmessage == CLIENTDISCONNECT)
	{
		if (EndMessage())
		{
			Serial.println("ESP lost connection to the client either with or without normal disconnect");
			clientConnected = false;
			Motors.setBrakes(0, 0);
		}
	}
	else if (espclientmessage == CLIENTPAUSED) {
		if (EndMessage())
		{
			Serial.println("ESP client is paused");
			clientConnected = false;
			Motors.setBrakes(0, 0);
		}
	}
	else if (espclientmessage == CLIENTCONTINUED) {
		if (EndMessage())
		{
			Serial.println("ESP client is continued");
			clientConnected = true;
		}
	}
}
#pragma endregion ReadSerialData

void HandleESPData()
{
	byte c = Serial3.read();
	Serial.print(c, HEX);
	Serial.print(" ");
	switch (c)
	{
	case COMMOTOR:
		ReadMotorData();
		break;
	case COMSERVO:
		ReadServoData();
		break;
	case COMCLIENT:
		ReadClientData();
		break;
	case COMGENERIC:
		ReadGenericData();
	case (byte)0x00:
		break;
	default:
		Serial.print(c, HEX);
		Serial.println(" is a unknown command");
		break;
	}
	Serial3.write(ESPMOTORSTAT);
	Serial3.write(M1Current);
	Serial3.write(M2Current);
	Serial3.write(MESSAGEEND);
}


void loop()
{
	currentMillis = millis();
	if (Serial3.available())
	{
		HandleESPData();
		Serial.println();
	}
	dofThread.check();
	connectionThread.check();
}
